// Logisim project cpu_benchmark.circ as structural Verilog
module cpu (
);

  wire ALU_output, and_1_out, and_2_out, beq, blez, bnq, Branch, clock_1_out, comparator_1_eq,
       comparator_1_gt, comparator_1_lt, condi_suc, Half_word, halt, or_1_out, PC_MUX_2, PC_MUX_3, RAM_LOAD,
       RAM_STO, register_ctrl_1_out_5, RST, syscall_t, un_Branch, wc, WE_t;
  wire [1:0] rA_t, rW_t, w_t, Y_t;
  wire [3:0] ALU_S;
  wire [4:0] register_ctrl_1_out_6, register_ctrl_1_out_7, register_ctrl_1_out_8;
  wire [7:0] PC_q_2;
  wire [11:0] npc, PC_q;
  wire [15:0] incrementer_1_p2, multiplexer_5_out, \周期数目 , \总周期数 , \无条件分支指令数 , \有条件分支成功跳转 , \有条件分支指令数 ;
  wire [19:0] alu_1_p4_2;
  wire [31:0] adder_1_out, alu_1_p4, bit_extender_1_out, bit_extender_2_out, bit_extender_3_out,
       bit_extender_4_out, instruction, mips_ram_1_p8, multiplexer_2_out, multiplexer_3_out,
       multiplexer_4_out, registerfile_1_p7, registerfile_1_p8, SyscallOut;

  Button \u_总复位  (.out(RST));
  Register #(.width(12)) PC (.D(npc), .en(halt), .Q({PC_q[11:10], PC_q_2, PC_q[1:0]}), .clk(clock_1_out), .clr(RST));
  assign bit_extender_1_out = {{20{1'b0}}, {PC_q[11:10], PC_q_2, PC_q[1:0]}};  // Bit_Extender bit_extender_1
  Clock clock_1 (.out(clock_1_out));
  Hex_Digit_Display hex_digit_display_1 (.value(SyscallOut[31:28]));  // open: dp
  Hex_Digit_Display hex_digit_display_2 (.value(SyscallOut[27:24]));  // open: dp
  // Incrementer incrementer_1: pin names not known; wires that end beside it: \周期数目 , incrementer_1_p2
  Hex_Digit_Display hex_digit_display_3 (.value(SyscallOut[19:16]));  // open: dp
  Hex_Digit_Display hex_digit_display_4 (.value(SyscallOut[23:20]));  // open: dp
  Adder #(.width(32)) adder_1 (.a(bit_extender_1_out), .b(32'h4), .out(adder_1_out), .cin(1'b0));  // open: cout
  ROM #(.dataWidth(32)) rom_1 (.addr(PC_q_2), .data(instruction));  // open: sel
  Counter #(.width(16), .max('hffff)) counter_1 (
    .load(1'b0), .count(halt), .Q(\周期数目 ), .clk(clock_1_out), .clr(RST));  // open: D, carry
  Multiplexer #(.width(16), .enable("false")) multiplexer_1 (
    .in0(incrementer_1_p2), .in1(\周期数目 ), .out(\总周期数 ), .sel(halt));
  Hex_Digit_Display hex_digit_display_5 (.value(SyscallOut[11:8]));  // open: dp
  Hex_Digit_Display hex_digit_display_6 (.value(SyscallOut[15:12]));  // open: dp
  Hex_Digit_Display hex_digit_display_7 (.value(SyscallOut[7:4]));  // open: dp
  Hex_Digit_Display hex_digit_display_8 (.value(SyscallOut[3:0]));  // open: dp
  assign bit_extender_2_out = {{16{instruction[15]}}, instruction[15:0]};  // Bit_Extender bit_extender_2
  register_ctrl register_ctrl_1 (
    .in_1(instruction), .in_3(rW_t), .in_2(rA_t), .in_4(WE_t), .out_5(register_ctrl_1_out_5),
    .out_6(register_ctrl_1_out_6), .out_7(register_ctrl_1_out_7), .out_8(register_ctrl_1_out_8));
  Multiplexer #(.select(2), .width(32), .enable("false")) multiplexer_2 (
    .in0({alu_1_p4[31:22], alu_1_p4_2, wc, alu_1_p4[0]}), .in1(adder_1_out), .in3(multiplexer_4_out),
    .out(multiplexer_2_out), .sel(w_t));  // open: in2
  controller controller_1 (
    .in_1(instruction), .Branch(Branch), .rw(rW_t), .Y(Y_t), .Half_word(Half_word), .un_Branch(un_Branch),
    .RAM_STO(RAM_STO), .Ra(rA_t), .ALU_S(ALU_S), .syscall(syscall_t), .PC_MUX_2(PC_MUX_2), .blez(blez),
    .WE(WE_t), .RAM_LOAD(RAM_LOAD), .PC_MUX_3(PC_MUX_3), .bnq(bnq), .w(w_t), .beq(beq),
    .ALU_output(ALU_output));
  Counter #(.width(16), .max('hffff)) counter_2 (
    .load(1'b0), .count(un_Branch), .Q(\无条件分支指令数 ), .clk(clock_1_out), .clr(RST));  // open: D, carry
  // Probe on \总周期数 
  // Probe on \无条件分支指令数 
  // Probe on \有条件分支指令数 
  // Probe on \有条件分支成功跳转 
  assign bit_extender_3_out = {{27{1'b0}}, instruction[10:6]};  // Bit_Extender bit_extender_3
  // RegisterFile registerfile_1: pin names not known; wires that end beside it: multiplexer_2_out, clock_1_out, register_ctrl_1_out_5, register_ctrl_1_out_6, register_ctrl_1_out_7, register_ctrl_1_out_8, registerfile_1_p7, registerfile_1_p8
  Comparator #(.width(32)) comparator_1 (
    .a(registerfile_1_p7), .b(32'ha), .gt(comparator_1_gt), .eq(comparator_1_eq), .lt(comparator_1_lt));
  Counter #(.width(16), .max('hffff)) counter_3 (
    .load(1'b0), .count(Branch), .Q(\有条件分支指令数 ), .clk(clock_1_out), .clr(RST));  // open: D, carry
  npc npc_1 (
    .in_1(instruction), .in_2(adder_1_out), .out_7(npc), .in_3(condi_suc), .in_4(PC_MUX_2), .in_5(PC_MUX_3),
    .in_6(registerfile_1_p7));
  Multiplexer #(.select(2), .width(32), .enable("false")) multiplexer_3 (
    .in0(registerfile_1_p8), .in1(bit_extender_3_out), .in3(bit_extender_2_out), .out(multiplexer_3_out),
    .sel(Y_t));  // open: in2
  or or_1 (or_1_out, comparator_1_gt, comparator_1_lt);
  // ALU alu_1: pin names not known; wires that end beside it: registerfile_1_p7, multiplexer_3_out, ALU_S, {alu_1_p4[31:22], alu_1_p4_2, wc, alu_1_p4[0]}
  Register #(.width(32)) register_1 (
    .D(registerfile_1_p8), .en(and_1_out), .Q(SyscallOut), .clk(clock_1_out), .clr(RST));
  and and_1 (and_1_out, or_1_out, syscall_t);
  and and_2 (and_2_out, comparator_1_eq, syscall_t);
  condi_jump condi_jump_1 (
    .in_1(registerfile_1_p7), .out_6(condi_suc), .in_4(multiplexer_3_out), .in_2(blez), .in_3(beq), .in_5(bnq));
  not not_1 (halt, and_2_out);
  Multiplexer #(.width(32), .enable("false")) multiplexer_4 (
    .in0(mips_ram_1_p8), .in1(bit_extender_4_out), .out(multiplexer_4_out), .sel(Half_word));
  // MIPS_RAM mips_ram_1: pin names not known; wires that end beside it: alu_1_p4_2, registerfile_1_p8, RAM_STO, 4'b1111, clock_1_out, RAM_LOAD, RST, mips_ram_1_p8
  Counter #(.width(16), .max('hffff)) counter_4 (
    .load(1'b0), .count(condi_suc), .Q(\有条件分支成功跳转 ), .clk(clock_1_out), .clr(RST));  // open: D, carry
  Multiplexer #(.width(16), .enable("false")) multiplexer_5 (
    .in0(mips_ram_1_p8[15:0]), .in1(mips_ram_1_p8[31:16]), .out(multiplexer_5_out), .sel(wc));
  assign bit_extender_4_out = {{16{multiplexer_5_out[15]}}, multiplexer_5_out};  // Bit_Extender bit_extender_4

  // Notes on the sheet:
  //   数码管输出应该用寄存器锁存，否则显示数据只能一闪而过
  //   可以通过项目增加Logisim库的方式将前几次实验完成的电路作为子电路引入到本电路中使用
  //   contents of rom_1 (hex, n*v repeats v):
  //   20110001 8100005 20110001 20120002 20130003 8100009 20110001 20120002 20130003 810000d 20110001
  //   20120002 20130003 8100011 20110001 20120002 20130003 c1000b8 20100001 20110001 118fc0 112020
  //   20020022 c 118882 12200001 8100015 112020 20020022 c 20110001 118880 112020 20020022 c 12200001
  //   810001f 20110001 118fc0 112020 20020022 c 1188c3 112020 20020022 c 118903 112020 20020022 c 118903
  //   112020 20020022 c 118903 112020 20020022 c 118903 112020 20020022 c 118903 112020 20020022 c 118903
  //   112020 20020022 c 118903 112020 20020022 c 20100001 109fc0 139fc3 8021 2012000c 24160003 26100001
  //   3210000f 20080008 20090001 139900 2709825 132020 20020022 c 1094022 1500fff9 22100001 2018000f
  //   2188024 108700 20080008 20090001 139902 2709825 132021 20020022 c 1094022 1500fff9 108702 2c9b022
  //   12c00001 8100050 4020 1084027 84400 3508ffff 82021 20020022 c 2010ffff 20110000 ae300000 22100001
  //   22310004 ae300000 22100001 22310004 ae300000 22100001 22310004 ae300000 22100001 22310004 ae300000
  //   22100001 22310004 ae300000 22100001 22310004 ae300000 22100001 22310004 ae300000 22100001 22310004
  //   ae300000 22100001 22310004 ae300000 22100001 22310004 ae300000 22100001 22310004 ae300000 22100001
  //   22310004 ae300000 22100001 22310004 ae300000 22100001 22310004 ae300000 22100001 22310004 ae300000
  //   22100001 22310004 22100001 8020 2011003c 8e130000 8e340000 274402a 11000002 ae330000 ae140000
  //   2231fffc 1611fff8 102020 20020022 c 22100004 2011003c 1611fff2 2002000a c 20100000 22100001 102020
  //   20020022 c 22100002 102020 20020022 c 22100003 102020 20020022 c 22100004 102020 20020022 c 22100005
  //   102020 20020022 c 22100006 102020 20020022 c 22100007 102020 20020022 c 22100008 102020 20020022
  //   20020022 c 3e00008
  //   数码管输出
  //   总复位信号应将除ROM以外所有存储组件全部清零
endmodule

module register_ctrl (
  input  [31:0] in_1,
  input  [1:0] in_2,
  input  [1:0] in_3,
  input  in_4,
  output out_5,
  output [4:0] out_6,
  output [4:0] out_7,
  output [4:0] out_8
);

  Multiplexer #(.select(2), .width(5), .enable("false")) multiplexer_1 (
    .in0(in_1[15:11]), .in1({5{1'b1}}), .in3(in_1[20:16]), .out(out_6), .sel(in_3));  // open: in2
  Multiplexer #(.select(2), .width(5), .enable("false")) multiplexer_2 (
    .in0(in_1[25:21]), .in1(5'b00010), .in3(in_1[20:16]), .out(out_7), .sel(in_2));  // open: in2
  Multiplexer #(.select(2), .width(5), .enable("false")) multiplexer_3 (
    .in0(in_1[20:16]), .in1(5'b00100), .in3(in_1[25:21]), .out(out_8), .sel(in_2));  // open: in2

  assign out_5 = in_4;

  // Other names for the same wires on the sheet: instruction[31:0] = in_1; rA[4:0] = out_7; rA_t[1:0] = in_2;
  //   rB[4:0] = out_8; rW[4:0] = out_6; rW_t[1:0] = in_3; WE = in_4; WE_t = in_4

  // Notes on the sheet:
  //   输入
  //   输出
endmodule

module condi_jump (
  input  [31:0] in_1,
  input  in_2,
  input  in_3,
  input  [31:0] in_4,
  input  in_5,
  output out_6
);

  wire and_1_out, and_2_out, and_3_out, comparator_1_eq, comparator_2_eq, comparator_2_lt, not_1_out,
       or_1_out;

  Comparator #(.width(32)) comparator_1 (.a(in_1), .b(in_4), .eq(comparator_1_eq));  // open: gt, lt
  Comparator #(.width(32)) comparator_2 (
    .a(in_1), .b({32{1'b0}}), .eq(comparator_2_eq), .lt(comparator_2_lt));  // open: gt
  or or_1 (or_1_out, comparator_2_eq, comparator_2_lt);
  not not_1 (not_1_out, comparator_1_eq);
  and and_1 (and_1_out, in_2, or_1_out);
  and and_2 (and_2_out, in_3, comparator_1_eq);
  and and_3 (and_3_out, in_5, not_1_out);
  or or_2 (out_6, and_1_out, and_2_out, and_3_out);

  // Other names for the same wires on the sheet: A[31:0] = in_1; B[31:0] = in_4; beq = in_3; blez = in_2; bnq = in_5;
  //   condi_suc = out_6
endmodule

module npc (
  input  [31:0] in_1,
  input  [31:0] in_2,
  input  in_3,
  input  in_4,
  input  in_5,
  input  [31:0] in_6,
  output [11:0] out_7
);

  wire [27:0] bit_extender_1_out, shifter_1_out;
  wire [31:0] adder_1_out, bit_extender_2_out, multiplexer_1_out, multiplexer_2_out, shifter_2_out;
  wire [31:12] multiplexer_3_out;

  assign bit_extender_1_out = {{2{1'b0}}, in_1[25:0]};  // Bit_Extender bit_extender_1
  assign bit_extender_2_out = {{16{in_1[15]}}, in_1[15:0]};  // Bit_Extender bit_extender_2
  Shifter #(.width(28)) shifter_1 (.in(bit_extender_1_out), .\dist (5'b00010), .out(shifter_1_out));
  Shifter #(.width(32)) shifter_2 (.in(bit_extender_2_out), .\dist (5'b00010), .out(shifter_2_out));
  Adder #(.width(32)) adder_1 (.a(in_2), .b(shifter_2_out), .out(adder_1_out), .cin(1'b0));  // open: cout
  Multiplexer #(.width(32), .enable("false")) multiplexer_1 (
    .in0(in_2), .in1(adder_1_out), .out(multiplexer_1_out), .sel(in_3));
  Multiplexer #(.width(32), .enable("false")) multiplexer_2 (
    .in0({in_2[3:0], shifter_1_out}), .in1(multiplexer_1_out), .out(multiplexer_2_out), .sel(in_4));
  Multiplexer #(.width(32), .enable("false")) multiplexer_3 (
    .in0(multiplexer_2_out), .in1(in_6), .out({multiplexer_3_out, out_7}), .sel(in_5));

  // Other names for the same wires on the sheet: pc_4[31:0] = in_2; npc[11:0] = out_7; A[31:0] = in_6;
  //   condi_suc = in_3; instruction[31:0] = in_1; PC_MUX_2 = in_4; PC_MUX_3 = in_5
endmodule
